# Fritzing sketch WiringDiagram (saved by Fritzing 0.9.3b)
breadboards: 1

parts:
  Raspberry_Pi_3_B+ = Raspberry Pi 3 [part_number=RPI-3-V1.2]
  NEMA_17_Stepper_Motor = Stepper Motor - Bipolar
  Stepper_Driver = DRV 8825 Stepper Motor Carrier, High Current [part_number="DRV 8825"]
  Left_Limit_Switch = Pushbutton [package=THT]
  Right_Limit_Switch = Pushbutton [package=THT]
  Wall_Power_Supply = DC Power [voltage=12V]
  USB_Power_Supply = DC Power [voltage=3.3V]  # not connected
  C1 = Electrolytic Capacitor [capacitance=1mF voltage=35V package="100 mil [THT, electrolytic]"]
  R1 = Resistor [tolerance=±5% resistance=1k package=THT]
  R2 = Resistor [tolerance=±5% resistance=1k package=THT]

nets:
  N1: Raspberry_Pi_3_B+.GND, Stepper_Driver.GROUND_LOG, Left_Limit_Switch.leg0, Right_Limit_Switch.leg0
  N2: Raspberry_Pi_3_B+.3V3, Stepper_Driver.RESET, Stepper_Driver.SLEEP, R1.Pin_1, R2.Pin_1
  N3: Raspberry_Pi_3_B+.GPIO24, Stepper_Driver.STEP
  N4: Raspberry_Pi_3_B+.GPIO23, Stepper_Driver.DIRECTION
  N5: Raspberry_Pi_3_B+.GPIO15, Left_Limit_Switch.leg1, R1.Pin_0
  N6: Raspberry_Pi_3_B+.GPIO14, Right_Limit_Switch.leg1, R2.Pin_0
  N7: NEMA_17_Stepper_Motor.A, Stepper_Driver.OUT_2B
  N8: NEMA_17_Stepper_Motor.C, Stepper_Driver.OUT_2A
  N9: NEMA_17_Stepper_Motor.B, Stepper_Driver.OUT_1A
  N10: NEMA_17_Stepper_Motor.D, Stepper_Driver.OUT_1B
  N11: Stepper_Driver.VOLTAGE_ST/_MT, Wall_Power_Supply.V+, C1.+
  N12: Stepper_Driver.GROUND_ST/_MT, Wall_Power_Supply.V-, C1.-
